// Logisim project part1.circ as structural Verilog: 1 circuit, main circuit main
module main (
);

  // Probe on 1'b1
  // Probe on 1'b0

  // Notes on the sheet:
  //   Vcc(5V)
  //   +
  //   -
  //   Gnd(0V)
  //   Logic Monitor
  //   High
  //   Low
endmodule
