// Logisim project part1-f2.circ as structural Verilog: 1 circuit, main circuit main
module main (
  input  a,
  input  b
);

  wire and_1_out, not_1_out, or_1_out, or_2_out;

  not not_1 (not_1_out, b);
  or or_1 (or_1_out, a, b);
  or or_2 (or_2_out, a, not_1_out);
  LED led_1 (.in(and_1_out));
  and and_1 (and_1_out, or_1_out, or_2_out);

  // Notes on the sheet:
  //   F
  //   2
endmodule
