// Logisim project exp.circ as structural Verilog: 3 circuits, main circuit part1
module part1 (
  input  A,
  input  B
);

  wire and_1_out, xor_1_out;

  xor xor_1 (xor_1_out, A, B);
  and and_1 (and_1_out, A, B);
  LED led_1 (.in(xor_1_out));
  LED #(.active("false")) led_2 (.in(xor_1_out));
  LED led_3 (.in(and_1_out));
  LED #(.active("false")) led_4 (.in(and_1_out));

  // Notes on the sheet:
  //   Logic Monitor
  //   Sum
  //   High
  //   Low
  //   Carry
  //   High
  //   Low
endmodule

module part2 (
  input  C_in,
  input  A,
  input  B
);

  wire and_1_out, and_2_out, or_1_out, xor_1_out, xor_2_out;

  xor xor_1 (xor_1_out, A, B);
  and and_1 (and_1_out, A, B);
  xor xor_2 (xor_2_out, C_in, xor_1_out);
  and and_2 (and_2_out, C_in, xor_1_out);
  LED led_1 (.in(xor_2_out));
  LED #(.active("false")) led_2 (.in(xor_2_out));
  LED led_3 (.in(or_1_out));
  or or_1 (or_1_out, and_2_out, and_1_out);
  LED #(.active("false")) led_4 (.in(or_1_out));

  // Notes on the sheet:
  //   Logic Monitor
  //   Sum
  //   Carry
  //   High
  //   Low
  //   High
  //   Low
endmodule

module part3 (
  input  Add_Subtract,
  input  B0,
  input  B1,
  input  B2,
  input  B3,
  input  A0,
  input  A1,
  input  A2,
  input  A3
);

  wire adder_1_cout;
  wire [3:0] adder_1_out, xor_1_out;

  xor xor_1 (xor_1_out[0], B0, Add_Subtract);
  xor xor_2 (xor_1_out[1], B1, Add_Subtract);
  xor xor_3 (xor_1_out[2], B2, Add_Subtract);
  xor xor_4 (xor_1_out[3], B3, Add_Subtract);
  Adder #(.width(4)) adder_1 (
    .a(xor_1_out), .b({A3, A2, A1, A0}), .out(adder_1_out), .cin(Add_Subtract), .cout(adder_1_cout));
  LED led_1 (.in(adder_1_out[0]));
  LED #(.active("false")) led_2 (.in(adder_1_out[0]));
  LED led_3 (.in(adder_1_out[1]));
  LED #(.active("false")) led_4 (.in(adder_1_out[1]));
  LED led_5 (.in(adder_1_out[2]));
  LED #(.active("false")) led_6 (.in(adder_1_out[2]));
  LED led_7 (.in(adder_1_out[3]));
  LED #(.active("false")) led_8 (.in(adder_1_out[3]));
  LED led_9 (.in(adder_1_cout));
  LED #(.active("false")) led_10 (.in(adder_1_cout));

  // Notes on the sheet:
  //   Logic Monitor
  //   C0
  //   High
  //   Low
  //   C1
  //   High
  //   Low
  //   C2
  //   High
  //   Low
  //   C3
  //   High
  //   Low
  //   Carry Out
  //   High
  //   Low
endmodule
